# Fritzing sketch agmad pcb fy eldomia (saved by Fritzing 0.9.3b)
circuit board: 8cm x 5cm
breadboards: 1

parts:
  J4 = female pin header, 3 pins [form="♀ (female)"]
  J5 = female pin header, 3 pins [form="♀ (female)"]
  J3 = female pin header, 3 pins [form="♀ (female)"]
  J1 = female pin header, 3 pins [form="♀ (female)"]
  J2 = female pin header, 3 pins [form="♀ (female)"]
  Part1 = Arduino Nano (Rev3.0)
  J6 = female pin header, 3 pins [form="♀ (female)"]
  J7 = female pin header, 3 pins [form="♀ (female)"]
  J8 = female pin header, 6 pins [form="♀ (female)"]
  J11 = female pin header, 3 pins [form="♀ (female)"]
  J10 = female pin header, 3 pins [form="♀ (female)"]
  JP1 = Header 2 [package=screwterminal-3.5mm-2_lock]
  J9 = female pin header, 2 pins [form="♀ (female)"]

nets:
  N1: J4.pin1, J5.pin1, J3.pin1, J1.pin1, J2.pin1, Part1.GND, J6.pin3, J7.pin3, J11.pin1, J10.pin1, JP1.1
  N2: J4.pin2, J5.pin2, J3.pin2, J1.pin2, J2.pin2, Part1.5V, J6.pin2, J7.pin2, J11.pin2, J10.pin2, J9.pin1, J9.pin2
  N3: J4.pin3, Part1.A5
  N4: J5.pin3, Part1.A3
  N5: J3.pin3, Part1.A4
  N6: J1.pin3, Part1.A2
  N7: J2.pin3, Part1.A6
  N8: Part1.D2, J7.pin1
  N9: Part1.D3, J6.pin1
  N10: Part1.D4, J8.pin1
  N11: Part1.D5, J8.pin2
  N12: Part1.D6, J8.pin3
  N13: Part1.D7, J8.pin4
  N14: Part1.D8, J8.pin5
  N15: Part1.D9, J8.pin6
  N16: Part1.VIN, JP1.2
  N17: Part1.A1, J11.pin3
  N18: Part1.A0, J10.pin3
